# Fritzing sketch DissenyDispositiu (saved by Fritzing 0.9.4)
circuit board: 7.82088cm x 4.55788cm
breadboards: 1

parts:
  Part1 = Adafruit FONA 808 Breakout [part_number="Adafruit #2542"]
  RL1 = Resistor [tolerance=±5% resistance=220 package=THT]
  R3 = Resistor [tolerance=±5% resistance=10k package=THT]
  RL2 = Resistor [tolerance=±5% resistance=220 package=THT]
  OMRON1 = OMRON PCB Power Relay – G5LE [part_number="G5LE-1\n" package=THT]
  DS1 = DS18B20 1-Wire Temperature Sensor [part_number=DS18B20]
  LED1 = LED - 5mm [color="Blue (525nm)" package="5 mm [THT]"]
  LED2 = LED - 5mm [color="Red (633nm)" package="5 mm [THT]"]
  P1 = Pushbutton [package="[THT]"]
  Part2 = CUSTOMAdafruit Pro Trinket 3.3V 12MHz [part_number="Adafruit #2010"]
  R4 = Resistor [tolerance=±5% resistance=4.7k package=THT]

nets:
  GND: Part1.GND, R3.Pin_1, OMRON1.COIL2, DS1.GND, LED1.cathode, LED2.cathode, Part2.GND
  VDD: Part1.Vio, DS1.VDD, P1.Pin_1, P1.Pin_2, Part2.+3V3, R4.Pin_1
  N1: Part1.RXD, Part2.D11
  N2: Part1.TXD, Part2.D12
  N3: Part1.RTS, Part2.D13
  N4: Part1.Key, Part2.D10
  N5: Part1.PwrStat, Part2.A0
  N6: Part1.NetStat, RL1.Pin_0
  N7: RL1.Pin_1, LED1.anode
  N8: R3.Pin_0, P1.Pin_3, P1.Pin_4, Part2.D3
  N9: RL2.Pin_0, Part2.D4
  N10: RL2.Pin_1, LED2.anode
  N11: OMRON1.COIL1, Part2.D5
  N12: DS1.DQ, Part2.D9, R4.Pin_0

notes:
  Espot-nik
  Calefaccio Remota
  GND
  BAT+
  D5
  RX
  TX

custom parts:
  Adafruit FONA 808 Breakout: Cellular + GPS tracking, all in one? Oh yes! Introducing Adafruit FONA 808 MiniGSM + GPS, an all-in-one cellular phone module with that lets you add location-tracking, voice, text, SMS and data to your project in an adorable little package.
  CUSTOMAdafruit Pro Trinket 3.3V 12MHz: AQUESTA PART NOMÉS TE CONNEXIONS PERMIETRALS: NO A7 I A6 I TAMPOC FTDI Trinket's got a big sister in town - the Pro Trinket 3V! Pro Trinket combines everything you love about Trinket with the familiarity of the core Arduino chip, the ATmega328. It's like an Arduino Pro Mini with more pins and USB tossed in. Trinket's a year old now, and while its been great to see tons of tiny projects,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
